// Logisim project ALU.circ as structural Verilog
module ALU (
  input  [31:0] in_1,
  input  [31:0] in_2,
  input  [3:0] Alu_select,
  input  [31:0] in_4,
  input  [31:0] in_5,
  input  [2:0] in_6,
  output [31:0] Alu_Result,
  output branch_output
);

  wire and_1_out, comparator_1_eq, comparator_1_gt, comparator_1_lt, comparator_2_eq, comparator_2_gt,
       comparator_2_lt, comparator_3_gt, comparator_4_gt, comparator_4_lt, not_2_out, not_3_out, not_4_out,
       not_5_out, not_6_out, Sign_Flag, slt_out, sltu_out, Zero_Flag;
  wire [31:0] adder_1_out, bit_extender_3_out, bit_extender_4_out, bit_extender_5_out, shifter_1_out,
       shifter_2_out, shifter_3_out, shifter_4_out;
  wire [63:0] bit_extender_1_out, bit_extender_2_out, multiplier_1_out;

  and and_1 (and_1_out, in_1[0], in_1[1], in_1[2], in_1[3], in_1[4], in_1[5], in_1[6], in_1[7], in_1[8], in_1[9], in_1[10], in_1[11], in_1[12], in_1[14], in_1[14], in_1[15], in_1[16], in_1[17], in_1[18], in_1[19], in_1[20], in_1[21], in_1[22], in_1[23], in_1[24], in_1[25], in_1[26], in_1[27], in_1[28], in_1[29], in_1[30], in_1[31]);
  not not_1 (Zero_Flag, and_1_out);
  // Probe on Zero_Flag
  Shifter #(.width(32)) shifter_1 (.in(in_2), .\dist (in_5[4:0]), .out(shifter_1_out));
  Shifter #(.shift("lr"), .width(32)) shifter_2 (.in(in_2), .\dist (in_5[4:0]), .out(shifter_2_out));
  Shifter #(.shift("ar"), .width(32)) shifter_3 (.in(in_2), .\dist (in_5[4:0]), .out(shifter_3_out));
  Shifter #(.shift("ar"), .width(32)) shifter_4 (.in(in_2), .\dist (in_5[4:0]), .out(shifter_4_out));
  Comparator #(.mode("unsigned"), .width(32)) comparator_1 (
    .a(in_2), .b({in_5[31:7], in_2[6], in_5[5:0]}), .gt(comparator_1_gt), .eq(comparator_1_eq),
    .lt(comparator_1_lt));
  Comparator #(.width(32)) comparator_2 (
    .a(in_2), .b({in_5[31:7], in_2[6], in_5[5:0]}), .gt(comparator_2_gt), .eq(comparator_2_eq),
    .lt(comparator_2_lt));
  Adder #(.width(32)) adder_1 (.a(in_2), .b(in_4), .out(adder_1_out));  // open: cin, cout
  assign bit_extender_1_out = {{32{in_2[31]}}, in_2};  // Bit_Extender bit_extender_1
  assign bit_extender_2_out = {{32{in_5[31]}}, {in_5[31:7], in_2[6], in_5[5:0]}};  // Bit_Extender bit_extender_2
  Comparator #(.width(32)) comparator_3 (
    .a(in_2), .b({in_5[31:7], in_2[6], in_5[5:0]}), .gt(comparator_3_gt), .lt(Sign_Flag));  // open: eq
  Comparator #(.mode("unsigned"), .width(32)) comparator_4 (
    .a(in_2), .b({in_5[31:7], in_2[6], in_5[5:0]}), .gt(comparator_4_gt), .lt(comparator_4_lt));  // open: eq
  not not_2 (not_2_out, comparator_1_gt);
  not not_3 (not_3_out, comparator_1_eq);
  not not_4 (not_4_out, comparator_2_gt);
  not not_5 (not_5_out, comparator_2_eq);
  assign bit_extender_3_out = {{31{1'b0}}, comparator_1_eq};  // Bit_Extender bit_extender_3
  Multiplier #(.width(64)) multiplier_1 (
    .a(bit_extender_1_out), .b(bit_extender_2_out), .out(multiplier_1_out));  // open: cin, cout
  // Probe on Sign_Flag
  and sltu (sltu_out, not_2_out, not_3_out, comparator_1_lt);
  and slt (slt_out, not_4_out, not_5_out, comparator_2_lt);
  assign bit_extender_4_out = {{31{1'b0}}, sltu_out};  // Bit_Extender bit_extender_4
  assign bit_extender_5_out = {{31{1'b0}}, slt_out};  // Bit_Extender bit_extender_5
  not not_6 (not_6_out, Zero_Flag);
  Multiplexer #(.enable("true"), .select(4), .width(32)) multiplexer_1 (
    .in4({in_1[31:14], in_1[14], in_1[12:0]}), .in5(shifter_1_out), .in6(shifter_2_out), .in7(shifter_3_out),
    .in8(shifter_4_out), .in9(bit_extender_4_out), .in10(bit_extender_5_out), .in11(bit_extender_3_out),
    .in12(adder_1_out), .in13({in_2[15:0], in_5[15:7], in_2[6], in_5[5:0]}), .in14(multiplier_1_out[31:0]),
    .out(Alu_Result), .sel(Alu_select));  // open: in0, in1, in2, in3, in15, en
  Multiplexer #(.enable("true"), .select(3)) multiplexer_2 (
    .in0(Zero_Flag), .in3(not_6_out), .in4(comparator_3_gt), .in5(Sign_Flag), .in6(comparator_4_gt),
    .in7(comparator_4_lt), .out(branch_output), .sel(in_6));  // open: in1, in2, en

  assign in_1[13] = in_1[14];
  assign in_5[6] = in_2[6];

  // Other names for the same wires on the sheet: B[31:0] = {in_5[31:7], in_2[6], in_5[5:0]}; B0 = in_5[0];
  //   least_significant_5_bits_of_B[4:0] = in_5[4:0];
  //   least_significant_16_bits_of_B[15:0] = {in_5[15:7], in_2[6], in_5[5:0]}; B1 = in_5[1]; B2 = in_5[2];
  //   B3 = in_5[3]; B4 = in_5[4]; B5 = in_5[5]; B7 = in_5[7]; B8 = in_5[8]; B9 = in_5[9]; B10 = in_5[10];
  //   B11 = in_5[11]; B12 = in_5[12]; B13 = in_5[13]; B14 = in_5[14]; B15 = in_5[15]; A[31:0] = in_2; A0 = in_2[0];
  //   A1 = in_2[1]; A2 = in_2[2]; A3 = in_2[3]; A4 = in_2[4]; A5 = in_2[5]; A6 = in_2[6]; A7 = in_2[7]; A8 = in_2[8];
  //   A9 = in_2[9]; A10 = in_2[10]; A11 = in_2[11]; A12 = in_2[12]; A13 = in_2[13]; A14 = in_2[14]; A15 = in_2[15];
  //   A16 = in_2[16]; A17 = in_2[17]; A18 = in_2[18]; A19 = in_2[19]; A20 = in_2[20]; A21 = in_2[21]; A22 = in_2[22];
  //   A23 = in_2[23]; A24 = in_2[24]; A25 = in_2[25]; A26 = in_2[26]; A27 = in_2[27]; A28 = in_2[28]; A29 = in_2[29];
  //   A30 = in_2[30]; A31 = in_2[31]; B16 = in_5[16]; B17 = in_5[17]; B18 = in_5[18]; B19 = in_5[19]; B20 = in_5[20];
  //   B21 = in_5[21]; B22 = in_5[22]; B23 = in_5[23]; B24 = in_5[24]; B25 = in_5[25]; B26 = in_5[26]; B27 = in_5[27];
  //   B28 = in_5[28]; B29 = in_5[29]; B30 = in_5[30]; B31 = in_5[31];
  //   Result[31:0] = {in_1[31:14], in_1[14], in_1[12:0]}; Rs1 = in_1[0]; Rs2 = in_1[1]; Rs3 = in_1[2]; Rs4 = in_1[3];
  //   Rs5 = in_1[4]; Rs6 = in_1[5]; Rs7 = in_1[6]; Rs8 = in_1[7]; Rs9 = in_1[8]; Rs10 = in_1[9]; Rs11 = in_1[10];
  //   Rs12 = in_1[11]; Rs13 = in_1[12]; Rs14 = in_1[14]; Rs15 = in_1[15]; Rs16 = in_1[16]; Rs17 = in_1[17];
  //   Rs18 = in_1[18]; Rs19 = in_1[19]; Rs20 = in_1[20]; Rs21 = in_1[21]; Rs22 = in_1[22]; Rs23 = in_1[23];
  //   Rs24 = in_1[24]; Rs25 = in_1[25]; Rs26 = in_1[26]; Rs27 = in_1[27]; Rs28 = in_1[28]; Rs29 = in_1[29];
  //   Rs30 = in_1[30]; Rs31 = in_1[31]

  // Notes on the sheet:
  //   seq
  //   set
  //   bge
  //   bgeu
  //   sset
  //   mul
  //   blt
  //   bleu
  //   beq
  //   bne
endmodule

module Alu_1_bit (
  input  A,
  input  B,
  input  CarryIn,
  input  BInvert,
  input  AInvert,
  input  [1:0] logic_Operation,
  output Result
);

  wire adder_1_cout, adder_1_out, and_1_out, multiplexer_1_out, multiplexer_2_out, not_1_out, not_2_out,
       or_1_out, xor_1_out;

  not not_1 (not_1_out, A);
  not not_2 (not_2_out, B);
  Multiplexer #(.enable("true")) multiplexer_1 (
    .in0(A), .in1(not_1_out), .out(multiplexer_1_out), .sel(AInvert));  // open: en
  Multiplexer #(.enable("true")) multiplexer_2 (
    .in0(B), .in1(not_2_out), .out(multiplexer_2_out), .sel(BInvert));  // open: en
  and and_1 (and_1_out, multiplexer_1_out, multiplexer_2_out);
  or or_1 (or_1_out, multiplexer_1_out, multiplexer_2_out);
  xor xor_1 (xor_1_out, multiplexer_1_out, multiplexer_2_out);
  Adder #(.width(1)) adder_1 (
    .a(multiplexer_1_out), .b(multiplexer_2_out), .out(adder_1_out), .cin(CarryIn), .cout(adder_1_cout));
  // Probe on adder_1_cout
  Multiplexer #(.enable("true"), .select(2)) multiplexer_3 (
    .in0(and_1_out), .in1(or_1_out), .in2(xor_1_out), .in3(adder_1_out), .out(Result), .sel(logic_Operation));  // open: en
endmodule
