// Logisim project EX_MEM_Register.circ as structural Verilog: 1 circuit, main circuit main
module main (
  input  in_1,
  input  in_2,
  input  [31:0] ALU_result_EX,
  input  [31:0] BusB_EX,
  input  MemRead_EX,
  input  MemWrite_EX,
  input  MemtoReg_EX,
  input  RegWrite_EX,
  input  [4:0] Reg_Des_EX,
  output [31:0] ALU_result_MEM,
  output [31:0] BusB_MEM,
  output MemRead_MEM,
  output MemWrite_MEM,
  output MemtoReg_MEM,
  output RegWrite_MEM,
  output [4:0] Reg_Des_MEM
);

  wire undriven, undriven_2;

  Register #(.width(32)) register_1 (.D(ALU_result_EX), .en(in_2), .clk(in_1), .Q(ALU_result_MEM));  // open: clr
  Register #(.width(1)) register_2 (.D(MemRead_EX), .en(in_2), .clk(in_1), .Q(MemRead_MEM));  // open: clr
  Register #(.width(1)) register_3 (.D(MemtoReg_EX), .en(in_2), .clk(in_1), .Q(MemtoReg_MEM));  // open: clr
  Register #(.width(5)) register_4 (.D(Reg_Des_EX), .en(in_2), .clk(in_1), .Q(Reg_Des_MEM));  // open: clr
  Register #(.width(32)) register_5 (.D(BusB_EX), .en(in_2), .clk(in_1), .Q(BusB_MEM), .clr(undriven));
  Register #(.width(1)) register_6 (.D(MemWrite_EX), .en(in_2), .clk(in_1), .Q(MemWrite_MEM), .clr(undriven_2));
  Register #(.width(1)) register_7 (.D(RegWrite_EX), .en(in_2), .clk(in_1), .Q(RegWrite_MEM));  // open: clr

  // Other names for the same wires on the sheet: CLK = in_1; EX_MEM_Enable = in_2
endmodule
