// Logisim project ForwardUnit1.circ as structural Verilog: 1 circuit, main circuit main
module main (
  input  MemRead_MEM,
  input  RegWrite_MEM,
  input  RegWrite_WB,
  input  [4:0] Reg_Des_WB,
  input  [4:0] Reg_Des_MEM,
  input  [4:0] Rs1_EX,
  input  [4:0] Rs2_EX,
  output [1:0] Forward
);

  wire and_2_out, comparator_1_eq, comparator_2_eq, comparator_3_eq, comparator_4_eq, comparator_5_eq,
       comparator_6_eq, comparator_7_eq, comparator_8_eq, Rs1_not_Zero, Rs2_not_Zero;

  Comparator #(.width(5), .mode("unsigned")) comparator_1 (
    .a(Rs1_EX), .b({5{1'b0}}), .eq(comparator_1_eq));  // open: gt, lt
  not not_1 (Rs1_not_Zero, comparator_1_eq);
  not not_2 (Rs2_not_Zero, comparator_2_eq);
  Comparator #(.width(5), .mode("unsigned")) comparator_2 (
    .a(Rs2_EX), .b({5{1'b0}}), .eq(comparator_2_eq));  // open: gt, lt
  Comparator #(.width(5), .mode("unsigned")) comparator_3 (
    .a(Rs2_EX), .b(Reg_Des_MEM), .eq(comparator_3_eq));  // open: gt, lt
  Comparator #(.width(5), .mode("unsigned")) comparator_4 (
    .a(Rs2_EX), .b(Reg_Des_MEM), .eq(comparator_4_eq));  // open: gt, lt
  Comparator #(.width(5), .mode("unsigned")) comparator_5 (
    .a(Rs2_EX), .b(Reg_Des_WB), .eq(comparator_5_eq));  // open: gt, lt
  Comparator #(.width(5), .mode("unsigned")) comparator_6 (
    .a(Rs1_EX), .b(Reg_Des_MEM), .eq(comparator_6_eq));  // open: gt, lt
  Comparator #(.width(5), .mode("unsigned")) comparator_7 (
    .a(Rs1_EX), .b(Reg_Des_WB), .eq(comparator_7_eq));  // open: gt, lt
  Comparator #(.width(5), .mode("unsigned")) comparator_8 (
    .a(Rs1_EX), .b(Reg_Des_MEM), .eq(comparator_8_eq));  // open: gt, lt
  and and_1 (Forward[0], RegWrite_MEM, comparator_6_eq, Rs1_not_Zero);
  and and_2 (and_2_out, ~Forward[0], RegWrite_WB, comparator_7_eq, Rs1_not_Zero);  // AND_Gate
  // AND_Gate and_3 has open pins: in0=Forward[0], in1=and_2_out, in2=MemRead_MEM, in3=RegWrite_MEM, in4=comparator_8_eq, in5=Rs1_not_Zero, out=open

  // Notes on the sheet:
  //   previous
  //   2nd previos
  //   LW
endmodule
