// Logisim project pc_circut.circ as structural Verilog: 1 circuit, main circuit main
module main (
  input  [10:0] upper11,
  input  [4:0] Lower5,
  input  in_3,
  input  in_4,
  input  [19:0] in_5,
  input  pc_circ,
  input  jalr,
  input  [15:0] IMM16,
  input  [31:0] RS1,
  output [19:0] pc_next
);

  wire [19:0] adder_2_out, adder_3_out, bit_extender_1_out, bit_extender_2_out, multiplexer_1_out, pc, pc_inc;

  // Probe on {upper11, Lower5}
  assign bit_extender_1_out = {{4{upper11[10]}}, {upper11, Lower5}};  // Bit_Extender bit_extender_1
  // Probe on pc
  Register #(.width(20)) register_1 (.D(pc_next), .en(in_3), .clk(in_4), .Q(pc));  // open: clr
  assign bit_extender_2_out = {{4{IMM16[15]}}, IMM16};  // Bit_Extender bit_extender_2
  // Probe on pc_inc
  Adder #(.width(20)) adder_1 (.a(pc), .b(in_5), .out(pc_inc), .cin(1'b0));  // open: cout
  Adder #(.width(20)) adder_2 (.a(bit_extender_1_out), .b(pc), .out(adder_2_out), .cin(1'b0));  // open: cout
  Adder #(.width(20)) adder_3 (.a(bit_extender_2_out), .b(RS1[19:0]), .out(adder_3_out), .cin(1'b0));  // open: cout
  // Probe on pc_next
  Multiplexer #(.width(20), .enable("false")) multiplexer_1 (
    .in0(pc_inc), .in1(adder_2_out), .out(multiplexer_1_out), .sel(pc_circ));
  Multiplexer #(.width(20), .enable("false")) multiplexer_2 (
    .in0(multiplexer_1_out), .in1(adder_3_out), .out(pc_next), .sel(jalr));
endmodule
